// Logisim project PART_1_LAB_4.circ as structural Verilog: 1 circuit, main circuit main
module main (
  input  A,
  input  [7:0] in_2,
  input  B,
  input  \Р0 ,
  input  in_5,
  input  [7:0] in_6,
  output [7:0] out_7,
  output P,
  output [7:0] out_9,
  output [7:0] out_10,
  output [7:0] out_11,
  output out_12,
  output S
);

  wire and_1_out, and_2_out, and_3_out, and_4_out, and_5_out, and_6_out, and_7_out, and_8_out, and_9_out,
       and_10_out, and_11_out, and_12_out, and_13_out, and_14_out, and_15_out, and_16_out, and_17_out,
       and_18_out, and_19_out, and_20_out, and_21_out, not_1_out, or_1_out, or_4_out, or_5_out, or_6_out,
       or_7_out, or_8_out, or_9_out, or_10_out, xor_1_out, xor_2_out, xor_3_out, xor_4_out, xor_5_out,
       xor_6_out, xor_7_out, xor_8_out;

  and and_1 (and_1_out, A, B);
  and and_2 (and_2_out, A, \Р0 );
  and and_3 (and_3_out, B, \Р0 );
  or or_1 (or_1_out, A, B, \Р0 );
  and and_4 (and_4_out, B, \Р0 , A);
  or or_2 (P, and_1_out, and_2_out, and_3_out);
  not not_1 (not_1_out, P);
  and and_5 (and_5_out, not_1_out, or_1_out);
  or or_3 (S, and_5_out, and_4_out);
  xor xor_1 (xor_1_out, in_2[0], in_6[0]);
  and and_6 (and_6_out, in_6[0], in_2[0]);
  xor xor_2 (xor_2_out, in_2[1], in_6[1]);
  and and_7 (and_7_out, in_6[1], in_2[1]);
  xor xor_3 (xor_3_out, in_2[2], in_6[2]);
  and and_8 (and_8_out, in_6[2], in_2[2]);
  xor xor_4 (xor_4_out, in_2[3], in_6[3]);
  and and_9 (and_9_out, in_6[3], in_2[3]);
  xor xor_5 (xor_5_out, in_2[4], in_6[4]);
  and and_10 (and_10_out, in_6[4], in_2[4]);
  xor xor_6 (xor_6_out, in_2[5], in_6[5]);
  and and_11 (and_11_out, in_6[5], in_2[5]);
  xor xor_7 (xor_7_out, in_2[6], in_6[6]);
  and and_12 (and_12_out, in_6[6], in_2[6]);
  xor xor_8 (xor_8_out, in_2[7], in_6[7]);
  and and_13 (and_13_out, in_6[7], in_2[7]);
  xor xor_9 (out_9[0], xor_1_out, in_5);
  and and_14 (and_14_out, xor_1_out, in_5);
  and and_15 (and_15_out, xor_2_out, or_4_out);
  and and_16 (and_16_out, xor_3_out, or_5_out);
  and and_17 (and_17_out, xor_4_out, or_6_out);
  and and_18 (and_18_out, xor_5_out, or_7_out);
  and and_19 (and_19_out, xor_6_out, or_8_out);
  and and_20 (and_20_out, xor_7_out, or_9_out);
  and and_21 (and_21_out, xor_8_out, or_10_out);
  or or_4 (or_4_out, and_14_out, and_6_out);
  xor xor_10 (out_9[1], xor_2_out, or_4_out);
  or or_5 (or_5_out, and_15_out, and_7_out);
  xor xor_11 (out_9[2], xor_3_out, or_5_out);
  or or_6 (or_6_out, and_16_out, and_8_out);
  xor xor_12 (out_9[3], xor_4_out, or_6_out);
  or or_7 (or_7_out, and_17_out, and_9_out);
  xor xor_13 (out_9[4], xor_5_out, or_7_out);
  or or_8 (or_8_out, and_18_out, and_10_out);
  xor xor_14 (out_9[5], xor_6_out, or_8_out);
  or or_9 (or_9_out, and_19_out, and_11_out);
  xor xor_15 (out_9[6], xor_7_out, or_9_out);
  or or_10 (or_10_out, and_20_out, and_12_out);
  xor xor_16 (out_9[7], xor_8_out, or_10_out);
  or or_11 (out_12, and_21_out, and_13_out);

  assign out_7 = in_2;
  assign out_10 = out_9;
  assign out_11 = in_6;

  // Notes on the sheet:
  //   A & B
  //   A & P0
  //   B & P0
  //   A | B | P0
  //   A & B & P0
  //   !P
  //   (A & B) | (A & P0) | (B & P0)
  //   (A | B | P0) & !P
  //   ((A | B | P0) & !P) | (A & B & P0)
endmodule
